# Fritzing sketch Chapelet_arduino (saved by Fritzing 0.9.3b)
breadboards: 3

parts:
  R1 = Resistor [tolerance=±5% resistance=150 package=THT]
  LED1 = LED - 5mm [color="Red (633nm)" package="5 mm [THT]"]
  LED3 = LED - 5mm [color="Red (633nm)" package="5 mm [THT]"]
  LED4 = LED - 5mm [color="Red (633nm)" package="5 mm [THT]"]
  Shift_Register = 74HC595 [package="DIP16 [THT]"]
  LED5 = LED - 5mm [color="Red (633nm)" package="5 mm [THT]"]
  LED6 = LED - 5mm [color="Red (633nm)" package="5 mm [THT]"]
  LED7 = LED - 5mm [color="Red (633nm)" package="5 mm [THT]"]
  LED8 = LED - 5mm [color="Red (633nm)" package="5 mm [THT]"]
  LED9 = LED - 5mm [color="Red (633nm)" package="5 mm [THT]"]
  LED10 = LED - 5mm [color="Red (633nm)" package="5 mm [THT]"]
  R2 = Resistor [tolerance=±5% resistance=150 package=THT]
  R3 = Resistor [tolerance=±5% resistance=150 package=THT]
  R4 = Resistor [tolerance=±5% resistance=150 package=THT]
  R5 = Resistor [tolerance=±5% resistance=150 package=THT]
  R6 = Resistor [tolerance=±5% resistance=150 package=THT]
  R7 = Resistor [tolerance=±5% resistance=150 package=THT]
  R8 = Resistor [tolerance=±5% resistance=150 package=THT]
  R9 = Resistor [tolerance=±5% resistance=220 package=THT]
  R10 = Resistor [tolerance=±5% resistance=150 package=THT]
  R11 = Resistor [tolerance=±5% resistance=1k package=THT]
  Arduino_Uno = Arduino Uno (Rev3)
  LED2 = LED - 5mm [color="Red (633nm)" package="5 mm [THT]"]
  U3 = Vibration Motor- ROB-08449 [package=vibe-motor-10mm]
  S3 = Pushbutton [package=THT]

nets (from the breadboard view):
  N1: R1.Pin_0, LED1.cathode
  N2: R1.Pin_1, Shift_Register.Q0
  N3: LED1.anode, LED3.anode, LED4.anode, Shift_Register.OE, LED5.anode, LED6.anode, LED7.anode, LED8.anode, LED9.anode, LED10.anode, R11.Pin_0, Arduino_Uno.GND, LED2.anode, U3.+
  N4: LED3.cathode, R3.Pin_0
  N5: LED4.cathode, R4.Pin_0
  N6: Shift_Register.Q1, R8.Pin_1
  N7: Shift_Register.Q2, R7.Pin_1
  N8: Shift_Register.Q3, R6.Pin_1
  N9: Shift_Register.Q4, R5.Pin_1
  N10: Shift_Register.Q5, R4.Pin_1
  N11: Shift_Register.Q6, R3.Pin_1
  N12: Shift_Register.Q7, R2.Pin_1
  N13: Shift_Register.SH_CP, Arduino_Uno.D9_PWM
  N14: Shift_Register.ST_CP, Arduino_Uno.D8
  N15: Shift_Register.DS, Arduino_Uno.D7
  VCC: Shift_Register.VCC, Arduino_Uno.5V, S3.leg1
  N16: LED5.cathode, R5.Pin_0
  N17: LED6.cathode, R6.Pin_0
  N18: LED7.cathode, R7.Pin_0
  N19: LED8.cathode, R8.Pin_0
  N20: LED9.cathode, R9.Pin_0
  N21: LED10.cathode, R10.Pin_0
  N22: R2.Pin_0, LED2.cathode
  N23: R9.Pin_1, Arduino_Uno.D13/SCK
  N24: R10.Pin_1, Arduino_Uno.D12/MISO
  N25: R11.Pin_1, Arduino_Uno.D2, S3.leg0
  N26: Arduino_Uno.D6_PWM, U3.-
